# Fritzing sketch AirHockey_schematic (saved by Fritzing 0.9.3b)

parts:
  M1 = EM705
  M3 = Stepper Motor - 8 wire
  M4 = Stepper Motor - 8 wire
  Mod1 = Raspberry Pi 4B
  Uart_5V_to_3_3V = Logic Level Converter [package="Breakout board"]
  36V_Power_Supply = prefix0000 [part_number="Meanwell, 36V, 17.5A, 630W"]
  24V_Power_Supply = prefix0000 [part_number="Meanwell, 24V, 6.25A, 150W"]
  5V_Power_Supply = prefix0000 [part_number="Meanwell, 5V, 3A, 15W"]
  M2 = EM705
  Bauteil1 = Arduino Leonardo (Rev3b)
  SWITCH_TB = D2F-FL Omron Snap Action Limit Switch with Level
  SWITCH_MID_L = D2F-FL Omron Snap Action Limit Switch with Level
  SWITCH_MID_R = D2F-FL Omron Snap Action Limit Switch with Level
  SWITCH_TB_2 = D2F-FL Omron Snap Action Limit Switch with Level
  R1 = Resistor [tolerance=±5% resistance=47k package=THT]
  R2 = Resistor [tolerance=±5% resistance=47k package=THT]
  R3 = Resistor [tolerance=±5% resistance=47k package=THT]
  R4 = Photocell (LDR) [package=THT]
  Mod2 = KY-008 Laser Transmitter Module [package="Breakout board"]  # not connected
  Mod3 = KY-008 Laser Transmitter Module [package="Breakout board"]  # not connected
  Solenoid_24V = Solenoid
  F1 = Fan - Ventilador [package=THT]
  SUNON_PMD2412PMB1-a(2)_GN = Fan - Ventilador [package=THT]
  LED_Goal_Human = White LED strip
  DFRobot_DFPlayer_Mini1 = DFRobot DFPlayer Mini [part_number=DFR0299]
  Visaton_FR10 = Loudspeaker
  Visaton_FR10_2 = Loudspeaker
  LED_Goal_Robot = White LED strip  # not connected
  KY-1 = Keyes Relay [package=THT]
  D1 = Diode [package=diode-1n4148]
  D2 = Diode [package=diode-1n4148]
  LED_Camera_Frame = White LED strip  # not connected
  LED_Matchfield = White LED strip  # not connected
  R4_2 = Resistor [tolerance=±5% resistance=1k package=THT]
  12V-24V_TPA33110_30W+30W = Adafruit MAX9744 20W Amplifier
  KY-2 = Keyes Relay [package=THT]
  C1 = Electrolytic Capacitor [capacitance=0.22mF voltage=40V package="300 mil [THT, electrolytic]"]
  D3 = Zener Diode [part_number=1N4732A breakdown_voltage=3.6V package="Melf DO-213 AB [SMD]"]
  SSR = Solid State High Level Relay Module [package=relay]
  Led_Driver = prefix0000 [part_number="Tridonic 60W"]
  R5 = Resistor [tolerance=±5% resistance=1k package=THT]
  R6 = Resistor [tolerance=±5% resistance=1k package=THT]
  R7 = Resistor [tolerance=±5% resistance=1k package=THT]
  R9 = Photocell (LDR) [package=THT]
  R8 = Resistor [tolerance=±5% resistance=1k package=THT]

nets (from the breadboard view):
  GND: M1.GND, 36V_Power_Supply.connector5, M2.GND
  N1: M1.+Vdc, 36V_Power_Supply.connector2, M2.+Vdc
  N2: M1.B-, M3.BLK, M3.WHT
  N3: M1.B+, M3.BRN, M3.ORG
  N4: M1.A-, M3.RED, M3.GRN
  N5: M1.A+, M3.BLU, M3.YEL
  N6: M1.FLT-, R6.Pin_0
  N7: M1.DIR-, M1.PUL-
  N8: M1.DIR+, Bauteil1.D4/A6
  N9: M1.PUL+, Bauteil1.D12/A11
  N10: M4.BLU, M4.YEL, M2.A+
  N11: M4.RED, M4.GRN, M2.A-
  N12: M4.BRN, M4.ORG, M2.B+
  N13: M4.BLK, M4.WHT, M2.B-
  5V: Mod1.5V, 5V_Power_Supply.connector2, Bauteil1.5V, R1.Pin_1, R2.Pin_1, R3.Pin_1
  N14: Mod1.GND, 5V_Power_Supply.connector5
  N15: Mod1.GPIO14, Uart_5V_to_3_3V.LV1
  N16: Mod1.GPIO15, Uart_5V_to_3_3V.LV2
  N17: Uart_5V_to_3_3V.HV2, Bauteil1.D1/TX
  N18: Uart_5V_to_3_3V.HV1, Bauteil1.D0/RX
  N19: 24V_Power_Supply.connector1, KY-1.NO
  N20: 24V_Power_Supply.connector4, C1.-
  N21: M2.FLT-, R5.Pin_0
  N22: M2.DIR-, M2.PUL-
  N23: M2.DIR+, Bauteil1.D6_PWM/A7
  N24: M2.PUL+, Bauteil1.D5_PWM
  N25: Bauteil1.D2/SDA, SWITCH_TB.COM, SWITCH_TB_2.COM, R1.Pin_0
  N26: Bauteil1.D3_PWM/SCL, Bauteil1.SCL, SWITCH_MID_R.COM, R2.Pin_0
  N27: Bauteil1.D7, SWITCH_MID_L.COM, R3.Pin_0
  N28: Bauteil1.D8/A8, KY-1.signal
  N29: Bauteil1.D9_PWM/A9, KY-2.signal
  N30: Bauteil1.D10_PWM/A10, DFRobot_DFPlayer_Mini1.TX
  N31: Bauteil1.D11_PWM, R4_2.Pin_0
  N32: Bauteil1.D13_PWM, SSR.CH1
  N33: SWITCH_TB.NO, SWITCH_MID_L.NO, SWITCH_MID_R.NO, SWITCH_TB_2.NO
  N34: R4.pin_1, R7.Pin_1
  N35: Solenoid_24V.pin2, KY-2.C, D3.cathode
  N36: F1.GND, D2.A
  N37: SUNON_PMD2412PMB1-a(2)_GN.5V, D1.C
  N38: SUNON_PMD2412PMB1-a(2)_GN.GND, D1.A
  N39: LED_Goal_Human.+24V, SSR.A1
  N40: LED_Goal_Human.-24V, Led_Driver.connector4
  N41: DFRobot_DFPlayer_Mini1.RX, R4_2.Pin_1
  N42: DFRobot_DFPlayer_Mini1.DAC_R, 12V-24V_TPA33110_30W+30W.RIGHTIN
  N43: DFRobot_DFPlayer_Mini1.DAC_L, 12V-24V_TPA33110_30W+30W.LEFTIN
  N44: DFRobot_DFPlayer_Mini1.GND-1, 12V-24V_TPA33110_30W+30W.AGND
  N45: Visaton_FR10.pin1, 12V-24V_TPA33110_30W+30W.RIGHT-
  N46: Visaton_FR10.pin2, 12V-24V_TPA33110_30W+30W.RIGHT+
  N47: Visaton_FR10_2.pin1, 12V-24V_TPA33110_30W+30W.LEFT-
  N48: Visaton_FR10_2.pin2, 12V-24V_TPA33110_30W+30W.LEFT+
  N49: SSR.B1, Led_Driver.connector2
  N50: R9.pin_1, R8.Pin_1

custom parts:
  EM705: EM704 2 phase Digital Stepper Drive 20-70V, 0.35-5A, Sensorless Stall Detection, Pre-Matching Motor
  Stepper Motor - 8 wire: Simple, but very powerful bi polar stepper motor. 8 wire
  Logic Level Converter: 5V to/from 3.3V logic level converter
  D2F-FL Omron Snap Action Limit Switch with Level: Snap action switch with stainless steel lever.
  KY-008 Laser Transmitter Module: KY-008 Laser Transmitter Module, emits a dot shaped red laser beam.
  Fan - Ventilador: Ventilador de 2 pines, se encuentra comunmente en computadoras de escritorio
  White LED strip: White led strip
  Keyes Relay: The Keyes 5V relay module is suitable for SCM development, home appliance control. It uses a 5V~12V TIL control signal which can control DC / AC signal.
  Adafruit MAX9744 20W Amplifier: Pump up the volume with this 20W stereo amplifier! This slim little board has a class D amplifier onboard that can drive 2 channels of 4-8 ohm impedance speakers at 20W each. Power it with 5-12VDC using the onboard DC power jack and plug stereo line level into the 3.5mm stereo headphone jack and jam out with ease. Since it's class D, its completely cool-running, no heat sinks are required and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
  Solid State High Level Relay Module: 5V Omron solid state relay 240V 2A output with resistance fuse.
